// Logisim project FP16_Adder_Group_4.circ as structural Verilog: 9 circuits, main circuit FPA
module FPA (
  input  [15:0] XA,
  input  [15:0] XB,
  output [15:0] RESULT,
  output OVF,
  output UNF
);

  wire IS_ZERO, OP, S_BIG, S_SMALL;
  wire [4:0] D, E_BIG, E_SMALL_UNUSED;
  wire [6:0] E_BIG7, E_D, E_N, E_R;
  wire [10:0] M_BIG, M_R, M_SMALL;
  wire [13:0] EXT_BIG, EXT_D, EXT_N, EXT_SMALL, M_BIG14;
  wire [14:0] SUM;
  wire [15:0] BIG, SMALL;

  COMPARE_SWAP compare_swap_1 (.XB(XB), .XA(XA), .SMALL(SMALL), .D(D), .BIG(BIG));
  UNPACK unpack_1 (.X(SMALL), .E(E_SMALL_UNUSED), .M(M_SMALL), .S(S_SMALL));
  UNPACK unpack_2 (.X(BIG), .E(E_BIG), .M(M_BIG), .S(S_BIG));
  DENORM denorm_1 (.E_IN(E_N), .EXT(EXT_N), .E_OUT(E_D), .EXT_OUT(EXT_D));
  xor xor_1 (OP, S_BIG, S_SMALL);
  assign M_BIG14 = {{3{1'b0}}, M_BIG};  // Bit_Extender bit_extender_1
  ALIGN align_1 (.D(D), .M_SMALL(M_SMALL), .EXT_SMALL(EXT_SMALL));
  ROUND round_1 (.E_IN(E_D), .EXT(EXT_D), .M(M_R), .E_OUT(E_R));
  Shifter #(.width(14)) shifter_1 (.in(M_BIG14), .\dist (4'b0011), .out(EXT_BIG));
  ADD_SUB add_sub_1 (.OP(OP), .EXT_BIG(EXT_BIG), .EXT_SMALL(EXT_SMALL), .SUM(SUM));
  assign E_BIG7 = {{2{1'b0}}, E_BIG};  // Bit_Extender bit_extender_2
  FLAGS_PACK flags_pack_1 (.E(E_R), .M(M_R), .IS_ZERO(IS_ZERO), .S(S_BIG), .RESULT(RESULT), .OVF(OVF), .UNF(UNF));
  NORMALIZE normalize_1 (.E_IN(E_BIG7), .SUM(SUM), .E_OUT(E_N), .IS_ZERO(IS_ZERO), .EXT(EXT_N));

  // Notes on the sheet:
  //   Step_1
  //   Step 2.1
  //   Step_2.2
  //   Step 7
  //   Step 2.3
  //   Step 3
  //   Step 4.1
  //   Step 6
  //   Step 4.2
  //   Step 4.3
  //   Step 5.1
  //   Step 8
  //   Step 5.2
endmodule

module UNPACK (
  input  [15:0] X,
  output S,
  output [4:0] E,
  output [10:0] M
);

  wire [15:0] E16, F16, M16, X_SH10, X_SH15;

  Shifter #(.shift("lr"), .width(16)) shifter_1 (.in(X), .\dist (4'b1111), .out(X_SH15));
  Shifter #(.shift("lr"), .width(16)) shifter_2 (.in(X), .\dist (4'b1010), .out(X_SH10));
  assign F16 = X & 16'h3ff;  // AND_Gate and_1, 16 bits wide
  assign E16 = X_SH10 & 16'h1f;  // AND_Gate and_2, 16 bits wide
  assign M16 = F16 | 16'h400;  // OR_Gate or_1, 16 bits wide
  Bit_Extender #(.in_width(16), .out_width(1), .\type ("zero")) bit_extender_1 (.in(X_SH15), .out(S));
  Bit_Extender #(.in_width(16), .out_width(5), .\type ("zero")) bit_extender_2 (.in(E16), .out(E));
  Bit_Extender #(.in_width(16), .out_width(11), .\type ("zero")) bit_extender_3 (.in(M16), .out(M));

  // Notes on the sheet:
  //   3
  //   6
  //   1
  //   4
  //   7
  //   2
  //   5
  //   8
endmodule

module COMPARE_SWAP (
  input  [15:0] XA,
  input  [15:0] XB,
  output [15:0] BIG,
  output [15:0] SMALL,
  output [4:0] D
);

  wire SB_TMP, SS_TMP, SWAP;
  wire [4:0] E_BIG, E_SMALL;
  wire [10:0] MB_TMP, MS_TMP;
  wire [15:0] MAGA, MAGB;

  UNPACK unpack_1 (.X(BIG), .E(E_BIG), .M(MB_TMP), .S(SB_TMP));
  assign MAGA = XA & 16'h7fff;  // AND_Gate and_1, 16 bits wide
  assign MAGB = XB & 16'h7fff;  // AND_Gate and_2, 16 bits wide
  Comparator #(.mode("unsigned"), .width(16)) comparator_1 (.a(MAGA), .b(MAGB), .lt(SWAP));  // open: gt, eq
  UNPACK unpack_2 (.X(SMALL), .E(E_SMALL), .M(MS_TMP), .S(SS_TMP));
  Multiplexer #(.width(16)) multiplexer_1 (.in0(XA), .in1(XB), .out(BIG), .sel(SWAP));
  Multiplexer #(.width(16)) multiplexer_2 (.in0(XB), .in1(XA), .out(SMALL), .sel(SWAP));
  Subtractor #(.width(5)) subtractor_1 (.a(E_BIG), .b(E_SMALL), .out(D), .bin(1'b0));  // open: bout

  // Notes on the sheet:
  //   6
  //   1
  //   3
  //   2
  //   7
  //   4
  //   5
  //   8
endmodule

module ALIGN (
  input  [10:0] M_SMALL,
  input  [4:0] D,
  output [13:0] EXT_SMALL
);

  wire D_SMALL, NO_LOSS, STICKY;
  wire [3:0] D4, SH;
  wire [13:0] EXT0, M14, SH_BACK, SH_R, STICKY14;

  Comparator #(.mode("unsigned"), .width(5)) comparator_1 (.a(D), .b(5'b01110), .lt(D_SMALL));  // open: gt, eq
  Bit_Extender #(.in_width(5), .out_width(4), .\type ("zero")) bit_extender_1 (.in(D), .out(D4));
  Multiplexer #(.width(4)) multiplexer_1 (.in0(4'b1111), .in1(D4), .out(SH), .sel(D_SMALL));
  assign M14 = {{3{1'b0}}, M_SMALL};  // Bit_Extender bit_extender_2
  Shifter #(.width(14)) shifter_1 (.in(M14), .\dist (4'b0011), .out(EXT0));
  Shifter #(.shift("lr"), .width(14)) shifter_2 (.in(EXT0), .\dist (SH), .out(SH_R));
  Shifter #(.width(14)) shifter_3 (.in(SH_R), .\dist (SH), .out(SH_BACK));
  assign STICKY14 = {{13{1'b0}}, STICKY};  // Bit_Extender bit_extender_3
  assign EXT_SMALL = SH_R | STICKY14;  // OR_Gate or_1, 14 bits wide
  Comparator #(.mode("unsigned"), .width(14)) comparator_2 (.a(EXT0), .b(SH_BACK), .eq(NO_LOSS));  // open: gt, lt
  not not_1 (STICKY, NO_LOSS);
endmodule

module ADD_SUB (
  input  OP,
  input  [13:0] EXT_BIG,
  input  [13:0] EXT_SMALL,
  output [14:0] SUM
);

  wire [14:0] ADD15, BIG15, SMALL15, SUB15;

  assign SMALL15 = {{1{1'b0}}, EXT_SMALL};  // Bit_Extender bit_extender_1
  Subtractor #(.width(15)) subtractor_1 (.a(BIG15), .b(SMALL15), .out(SUB15), .bin(1'b0));  // open: bout
  assign BIG15 = {{1{1'b0}}, EXT_BIG};  // Bit_Extender bit_extender_2
  Adder #(.width(15)) adder_1 (.a(BIG15), .b(SMALL15), .out(ADD15), .cin(1'b0));  // open: cout
  Multiplexer #(.width(15)) multiplexer_1 (.in0(ADD15), .in1(SUB15), .out(SUM), .sel(OP));
endmodule

module NORMALIZE (
  input  [14:0] SUM,
  input  [6:0] E_IN,
  output [13:0] EXT,
  output [6:0] E_OUT,
  output IS_ZERO
);

  wire ANY, CARRY, NOT_ANY, NOT_CARRY, SUM_BIT0;
  wire [3:0] K, P;
  wire [6:0] E_A, E_B, E_PRE, K7;
  wire [13:0] EXT_A, EXT_B, LOW14, RIGHT14, SUM_BIT0_14;
  wire [14:0] SUM_R15, SUM_SH14;

  Bit_Extender #(.in_width(15), .out_width(14), .\type ("zero")) bit_extender_1 (.in(SUM), .out(LOW14));
  Shifter #(.shift("lr"), .width(15)) shifter_1 (.in(SUM), .\dist (4'b0001), .out(SUM_R15));
  Bit_Extender #(.in_width(15), .out_width(1), .\type ("zero")) bit_extender_2 (.in(SUM), .out(SUM_BIT0));
  Bit_Extender #(.in_width(15), .out_width(14), .\type ("zero")) bit_extender_3 (.in(SUM_R15), .out(RIGHT14));
  assign SUM_BIT0_14 = {{13{1'b0}}, SUM_BIT0};  // Bit_Extender bit_extender_4
  BitFinder #(.\type ("high1"), .width(14)) bitfinder_1 (.in(LOW14), .index(P), .found(ANY));
  Shifter #(.shift("lr"), .width(15)) shifter_2 (.in(SUM), .\dist (4'b1110), .out(SUM_SH14));
  assign EXT_A = RIGHT14 | SUM_BIT0_14;  // OR_Gate or_1, 14 bits wide
  Subtractor #(.width(4)) subtractor_1 (.a(4'b1101), .b(P), .out(K), .bin(1'b0));  // open: bout
  Bit_Extender #(.in_width(15), .out_width(1), .\type ("zero")) bit_extender_5 (.in(SUM_SH14), .out(CARRY));
  Adder #(.width(7)) adder_1 (.a(E_IN), .b(7'b0000001), .out(E_A), .cin(1'b0));  // open: cout
  Multiplexer #(.width(14)) multiplexer_1 (.in0(EXT_B), .in1(EXT_A), .out(EXT), .sel(CARRY));
  Shifter #(.width(14)) shifter_3 (.in(LOW14), .\dist (K), .out(EXT_B));
  not not_1 (NOT_ANY, ANY);
  not not_2 (NOT_CARRY, CARRY);
  assign K7 = {{3{1'b0}}, K};  // Bit_Extender bit_extender_6
  and and_1 (IS_ZERO, NOT_ANY, NOT_CARRY);
  Multiplexer #(.width(7)) multiplexer_2 (.in0(E_B), .in1(E_A), .out(E_PRE), .sel(CARRY));
  Multiplexer #(.width(7)) multiplexer_3 (.in0(E_PRE), .in1(E_IN), .out(E_OUT), .sel(IS_ZERO));
  Subtractor #(.width(7)) subtractor_2 (.a(E_IN), .b(K7), .out(E_B), .bin(1'b0));  // open: bout
endmodule

module ROUND (
  input  [13:0] EXT,
  input  [6:0] E_IN,
  output [10:0] M,
  output [6:0] E_OUT
);

  wire G, LSB, R, ROUND_CARRY, ROUNDUP, RS, RSL, S_BIT;
  wire [10:0] M0, M1;
  wire [13:0] EXT_SH1, EXT_SH2, EXT_SH3;

  Shifter #(.shift("lr"), .width(14)) shifter_1 (.in(EXT), .\dist (4'b0010), .out(EXT_SH2));
  Bit_Extender #(.in_width(14), .out_width(1), .\type ("zero")) bit_extender_1 (.in(EXT_SH1), .out(R));
  Shifter #(.shift("lr"), .width(14)) shifter_2 (.in(EXT), .\dist (4'b0001), .out(EXT_SH1));
  Bit_Extender #(.in_width(14), .out_width(1), .\type ("zero")) bit_extender_2 (.in(EXT), .out(S_BIT));
  Bit_Extender #(.in_width(11), .out_width(1), .\type ("zero")) bit_extender_3 (.in(M0), .out(LSB));
  Shifter #(.shift("lr"), .width(14)) shifter_3 (.in(EXT), .\dist (4'b0011), .out(EXT_SH3));
  Bit_Extender #(.in_width(14), .out_width(1), .\type ("zero")) bit_extender_4 (.in(EXT_SH2), .out(G));
  Bit_Extender #(.in_width(14), .out_width(11), .\type ("zero")) bit_extender_5 (.in(EXT_SH3), .out(M0));
  or or_1 (RS, R, S_BIT);
  or or_2 (RSL, RS, LSB);
  and and_1 (ROUNDUP, G, RSL);
  Adder #(.width(11)) adder_1 (.a(M0), .b({11{1'b0}}), .out(M1), .cin(ROUNDUP), .cout(ROUND_CARRY));
  Multiplexer #(.width(11)) multiplexer_1 (.in0(M1), .in1(11'h400), .out(M), .sel(ROUND_CARRY));
  Adder #(.width(7)) adder_2 (.a(E_IN), .b({7{1'b0}}), .out(E_OUT), .cin(ROUND_CARRY));  // open: cout
endmodule

module DENORM (
  input  [13:0] EXT,
  input  [6:0] E_IN,
  output [13:0] EXT_OUT,
  output [6:0] E_OUT
);

  wire IS_SUB, SAME, STICKY;
  wire [3:0] SH4;
  wire [6:0] SH7;
  wire [13:0] BACK, DEN, SHR, ST14;

  Subtractor #(.width(7)) subtractor_1 (.a(7'b0000001), .b(E_IN), .out(SH7), .bin(1'b0));  // open: bout
  Comparator #(.width(14)) comparator_1 (.a(EXT), .b(BACK), .eq(SAME));  // open: gt, lt
  Comparator #(.width(7)) comparator_2 (.a(E_IN), .b(7'b0000001), .lt(IS_SUB));  // open: gt, eq
  assign DEN = SHR | ST14;  // OR_Gate or_1, 14 bits wide
  not not_1 (STICKY, SAME);
  assign ST14 = {{13{1'b0}}, STICKY};  // Bit_Extender bit_extender_1
  Bit_Extender #(.in_width(7), .out_width(4), .\type ("zero")) bit_extender_2 (.in(SH7), .out(SH4));
  Shifter #(.shift("lr"), .width(14)) shifter_1 (.in(EXT), .\dist (SH4), .out(SHR));
  Shifter #(.width(14)) shifter_2 (.in(SHR), .\dist (SH4), .out(BACK));
  Multiplexer #(.width(14)) multiplexer_1 (.in0(EXT), .in1(DEN), .out(EXT_OUT), .sel(IS_SUB));
  Multiplexer #(.width(7)) multiplexer_2 (.in0(E_IN), .in1(7'b0000001), .out(E_OUT), .sel(IS_SUB));

  // Other names for the same wires on the sheet: E_O[6:0] = E_OUT; EXT_O[13:0] = EXT_OUT
endmodule

module FLAGS_PACK (
  input  S,
  input  [6:0] E,
  input  [10:0] M,
  input  IS_ZERO,
  output [15:0] RESULT,
  output OVF,
  output UNF
);

  wire IS_INF, LT31, M10, NZ, SUBN;
  wire [4:0] E5, E5_N, E5_RAW;
  wire [9:0] F10, F10_RAW;
  wire [10:0] M_SH10;
  wire [15:0] E16, E_FIELD, F16, PACKED, S16, S_FIELD;

  assign S16 = {{15{1'b0}}, S};  // Bit_Extender bit_extender_1
  Multiplexer #(.width(10)) multiplexer_1 (.in0(F10_RAW), .in1({10{1'b0}}), .out(F10), .sel(IS_INF));
  Bit_Extender #(.in_width(7), .out_width(5), .\type ("zero")) bit_extender_2 (.in(E), .out(E5_RAW));
  Multiplexer #(.width(5)) multiplexer_2 (.in0(E5_RAW), .in1({5{1'b0}}), .out(E5_N), .sel(SUBN));
  Comparator #(.width(7)) comparator_1 (.a(E), .b(7'b0011111), .lt(LT31));  // open: gt, eq
  Shifter #(.shift("lr"), .width(11)) shifter_1 (.in(M), .\dist (4'b1010), .out(M_SH10));
  Bit_Extender #(.in_width(11), .out_width(10), .\type ("zero")) bit_extender_3 (.in(M), .out(F10_RAW));
  assign F16 = {{6{1'b0}}, F10};  // Bit_Extender bit_extender_4
  Shifter #(.width(16)) shifter_2 (.in(S16), .\dist (4'b1111), .out(S_FIELD));
  not not_1 (IS_INF, LT31);
  Bit_Extender #(.in_width(11), .out_width(1), .\type ("zero")) bit_extender_5 (.in(M_SH10), .out(M10));
  not not_2 (SUBN, M10);
  Multiplexer #(.width(5)) multiplexer_3 (.in0(E5_N), .in1({5{1'b1}}), .out(E5), .sel(IS_INF));
  Shifter #(.width(16)) shifter_3 (.in(E16), .\dist (4'b1010), .out(E_FIELD));
  not not_3 (NZ, IS_ZERO);
  assign E16 = {{11{1'b0}}, E5};  // Bit_Extender bit_extender_6
  and and_1 (UNF, SUBN, NZ, LT31);
  assign PACKED = S_FIELD | E_FIELD | F16;  // OR_Gate or_1, 16 bits wide
  and and_2 (OVF, IS_INF, NZ);
  Multiplexer #(.width(16)) multiplexer_4 (.in0(PACKED), .in1({16{1'b0}}), .out(RESULT), .sel(IS_ZERO));

  // Other names for the same wires on the sheet: OVF_I = OVF; RESULT_I[15:0] = RESULT; UNF_I = UNF
endmodule
